// Logisim project adder.circ as structural Verilog: 3 circuits, main circuit main
module main (
  input  in_1,
  input  in_2,
  input  in_3,
  input  in_4,
  input  in_5,
  input  in_6,
  input  in_7,
  input  in_8,
  input  in_9,
  output out_10,
  output out_11,
  output out_12,
  output out_13
);

  wire full_adder_2_cout, full_adder_3_cout, full_adder_4_cout, xor_1_out, xor_2_out, xor_3_out, xor_4_out;

  full_adder full_adder_1 (.A(in_6), .B(xor_2_out), .Cin(full_adder_2_cout), .S(out_10));  // open: Cout
  full_adder full_adder_2 (.A(in_7), .B(xor_1_out), .Cin(full_adder_3_cout), .Cout(full_adder_2_cout), .S(out_11));
  full_adder full_adder_3 (.A(in_8), .B(xor_3_out), .Cin(full_adder_4_cout), .Cout(full_adder_3_cout), .S(out_12));
  full_adder full_adder_4 (.A(in_9), .B(xor_4_out), .Cin(in_5), .Cout(full_adder_4_cout), .S(out_13));
  xor xor_1 (xor_1_out, in_2, in_5);
  xor xor_2 (xor_2_out, in_1, in_5);
  xor xor_3 (xor_3_out, in_3, in_5);
  xor xor_4 (xor_4_out, in_4, in_5);
endmodule

module half_adder (
  input  A,
  input  B,
  output C,
  output S
);

  and and_1 (C, A, B);
  xor xor_1 (S, A, B);
endmodule

module full_adder (
  input  A,
  input  B,
  input  Cin,
  output Cout,
  output S
);

  wire AB_out, AC_out, BC_out, xor_1_out;

  and AB (AB_out, A, B);
  and AC (AC_out, A, Cin);
  or or_1 (Cout, AB_out, AC_out, BC_out);
  and BC (BC_out, B, Cin);
  xor xor_1 (xor_1_out, A, B);
  xor xor_2 (S, xor_1_out, Cin);
endmodule
