// Logisim project sop.circ as structural Verilog: 1 circuit, main circuit main
module main (
  input  A,
  input  B,
  input  C,
  input  A_2,
  input  B_2,
  input  C_2,
  output out_7,
  output out_8
);

  wire and_1_out, and_2_out, and_3_out, and_4_out, and_5_out, and_6_out, and_7_out, and_8_out;

  and and_1 (and_1_out, ~A, ~B);  // AND_Gate
  and and_2 (and_2_out, and_1_out, C);
  and and_3 (and_3_out, A, ~B);  // AND_Gate
  and and_4 (and_4_out, and_3_out, C);
  or or_1 (out_8, and_2_out, and_4_out, and_6_out);
  and and_5 (and_5_out, A, B);
  and and_6 (and_6_out, and_5_out, C);
  and and_7 (and_7_out, ~B_2, C_2);  // AND_Gate
  and and_8 (and_8_out, A_2, C_2);
  or or_2 (out_7, and_8_out, and_7_out);

  // Notes on the sheet:
  //   (!A + A)!BC
  //   (1)!BC
  //   !BC
  //   !A!BC + A!BC + ABC
  //   (!B + B)AC
  //   (1)AC
  //   AC
  //   !BC + AC
  //   !BC + AC
endmodule
