// Logisim project table1.circ as structural Verilog: 1 circuit, main circuit main
module main (
  input  a,
  input  b,
  input  c,
  input  d,
  output out_5
);

  wire and_1_out, and_2_out;

  and and_1 (and_1_out, a, c, d);
  and and_2 (and_2_out, ~b, ~d);  // AND_Gate
  or or_1 (out_5, and_1_out, and_2_out);

  // Notes on the sheet:
  //   ACD + !B!D
endmodule
