// Logisim project table2.circ as structural Verilog: 1 circuit, main circuit main
module main (
  input  a,
  input  b,
  input  c,
  input  d,
  output out_5
);

  wire and_1_out, and_2_out, and_3_out;

  and and_1 (and_1_out, ~a, ~d);  // AND_Gate
  and and_2 (and_2_out, a, b, c, d);
  or or_1 (out_5, and_1_out, and_2_out, and_3_out);
  and and_3 (and_3_out, ~b, ~c);  // AND_Gate

  // Notes on the sheet:
  //   ABCD + !B!C + !A!D
endmodule
